# Fritzing sketch Pop Rockets (saved by Fritzing 1.0.4)
breadboards: 1

parts:
  Part2 = Arduino MKR ENV Shield  # not connected
  Part1 = Arduino MKR WIFI 1010  # not connected
  M1 = Arduino NANO RP2040 CONNECT with headers
  Part3 = Arduino Uno (Rev3)  # not connected

nets:
  N1: M1.GND-4, M1.GND-29

custom parts:
  Arduino MKR ENV Shield: The MKR ENV Shield allows a MKR board to acquire environmental data collected by an array of sensors. These sensors are of the latest generation and measure: Atmospheric pressure Temperature and humidity Ultraviolet UVA intensity Ultraviolet UVB intensity, UV Index (calculated) Light intensity (in LUX) To help you build projects and store the data collected locally, this shield has a slot for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
  Arduino MKR WIFI 1010: The MKR WIFI 1010 is a significant improvement on the MKR 1000 WIFI. It's equipped with an ESP32 module made by U-BLOX. This board aims to speed up and simplify the prototyping of WiFi based IoT applications thanks to the flexibility of the ESP32 module and its low power consumption. The board is composed of three main blocks: SAMD21 Cortex-M0+ 32bit Low Power ARM MCU; U-BLOX NINA-W10 Series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
